// Logisim project Binary Adder.circ as structural Verilog: 2 circuits, main circuit Half Adder
// HA
module Half_Adder (
  input  A,
  input  B,
  output Sum,
  output Cout
);

  xor xor_1 (Sum, A, B);
  and and_1 (Cout, A, B);
endmodule

module Full_Adder (
  input  Cin,
  input  A,
  input  B,
  output S,
  output Cout
);

  wire half_adder_1_cout, half_adder_1_sum, half_adder_2_cout;

  Half_Adder half_adder_1 (.A(A), .B(B), .Sum(half_adder_1_sum), .Cout(half_adder_1_cout));
  Half_Adder half_adder_2 (.A(Cin), .B(half_adder_1_sum), .Sum(S), .Cout(half_adder_2_cout));
  or or_1 (Cout, half_adder_2_cout, half_adder_1_cout);
endmodule
